// Logisim project Fibonacci_3.circ as structural Verilog: 2 circuits, main circuit main
module main (
  input  in_1,
  input  [2:0] in_2,
  output [7:0] out_3
);

  wire clk, comparator_1_eq, comparator_1_lt, counter_3_q, not_1_out, or_1_out, reset;
  wire [1:0] counter_1_q, counter_4_q;
  wire [3:0] bit_extender_1_out, counter_2_q;
  wire [7:0] adder_1_out_4, multiplexer_1_out, multiplexer_2_out, multiplexer_3_out, n_1_q, n_2_q, n_q,
       register_1_q;

  Clock clock_1 (.out(clk));
  Counter #(.width(2), .max('h3), .ongoal("stay")) counter_1 (
    .Q(counter_1_q), .clk(clk), .clr(reset));  // open: load, D, count, carry
  assign bit_extender_1_out = {{1{1'b0}}, in_2};  // Bit_Extender bit_extender_1
  Counter #(.width(4), .max('hf), .ongoal("stay")) counter_2 (
    .Q(counter_2_q), .clk(clk), .clr(reset));  // open: load, D, count, carry
  Multiplexer #(.select(2), .width(8)) multiplexer_1 (
    .in0({8{1'b0}}), .in1({8{1'b0}}), .in2({8{1'b0}}), .in3(n_2_q), .out(multiplexer_1_out), .sel(counter_1_q));  // open: en
  Comparator #(.width(4), .mode("unsigned")) comparator_1 (
    .a(bit_extender_1_out), .b(counter_2_q), .eq(comparator_1_eq), .lt(comparator_1_lt));  // open: gt
  Counter #(.width(1), .max('h1), .ongoal("stay")) counter_3 (
    .Q(counter_3_q), .clk(clk), .clr(reset));  // open: load, D, count, carry
  // Probe on adder_1_out_4
  adder adder_1 (.in_1(multiplexer_1_out), .in_2(multiplexer_3_out), .in_3(multiplexer_2_out), .out_4(adder_1_out_4));
  Multiplexer #(.width(8)) multiplexer_2 (
    .in0(8'h1), .in1(n_q), .out(multiplexer_2_out), .sel(counter_3_q));  // open: en
  or or_1 (or_1_out, comparator_1_eq, comparator_1_lt);
  // Probe on n_q
  Register n (.D(adder_1_out_4), .Q(n_q), .clk(clk), .clr(reset));  // open: en
  // Probe on n_1_q
  Register n_1 (.D(n_q), .Q(n_1_q), .clk(clk), .clr(reset));  // open: en
  not not_1 (not_1_out, or_1_out);
  Register n_2 (.D(n_1_q), .Q(n_2_q), .clk(clk), .clr(reset));  // open: en
  Counter #(.width(2), .max('h2), .ongoal("stay")) counter_4 (
    .Q(counter_4_q), .clk(clk), .clr(reset));  // open: load, D, count, carry
  // Probe on n_2_q
  Multiplexer #(.select(2), .width(8)) multiplexer_3 (
    .in0({8{1'b0}}), .in1({8{1'b0}}), .in2(n_1_q), .out(multiplexer_3_out), .sel(counter_4_q));  // open: in3, en
  Counter #(.width(1), .max('h1), .ongoal("stay")) counter_5 (
    .count(in_1), .Q(reset), .clk(clk), .clr(reset));  // open: load, D, carry
  Register register_1 (.D(adder_1_out_4), .en(not_1_out), .Q(register_1_q), .clk(clk), .clr(reset));
  Multiplexer #(.width(8)) multiplexer_4 (
    .in0({8{1'b0}}), .in1(register_1_q), .out(out_3), .sel(or_1_out));  // open: en
endmodule

module adder (
  input  [7:0] in_1,
  input  [7:0] in_2,
  input  [7:0] in_3,
  output [7:0] out_4
);

  wire [7:0] adder_1_out;

  Adder adder_1 (.a(in_1), .b(in_2), .out(adder_1_out));  // open: cin, cout
  Adder adder_2 (.a(adder_1_out), .b(in_3), .out(out_4));  // open: cin, cout
endmodule
