// Logisim project P0_L0_CRC.circ as structural Verilog: 2 circuits, main circuit CRC
module _2bit_mod2 (
  input  [3:0] dividee,
  input  [3:0] divider,
  output quotient,
  output [2:0] Remainder
);

  wire and_1_out, and_2_out, and_3_out;

  and and_1 (and_1_out, dividee[3], divider[0]);
  and and_2 (and_2_out, dividee[3], divider[1]);
  and and_3 (and_3_out, dividee[3], divider[2]);
  xor xor_1 (Remainder[0], dividee[0], and_1_out);
  xor xor_2 (Remainder[1], dividee[1], and_2_out);
  xor xor_3 (Remainder[2], dividee[2], and_3_out);

  assign quotient = dividee[3];
endmodule

module CRC (
  input  [7:0] A,
  input  [3:0] B,
  output [10:0] out_3
);

  wire [2:0] n2bit_mod2_1_remainder, n2bit_mod2_2_remainder, n2bit_mod2_3_remainder, n2bit_mod2_5_remainder,
       n2bit_mod2_6_remainder, n2bit_mod2_7_remainder;
  wire [3:1] low_half;

  // Probe on {A, 3'b000}
  _2bit_mod2 u_2bit_mod2_1 (
    .dividee({low_half, A[2]}), .divider(B), .Remainder(n2bit_mod2_1_remainder));  // open: quotient
  _2bit_mod2 u_2bit_mod2_2 (
    .dividee({n2bit_mod2_1_remainder, A[1]}), .divider(B), .Remainder(n2bit_mod2_2_remainder));  // open: quotient
  _2bit_mod2 u_2bit_mod2_3 (.dividee(A[7:4]), .divider(B), .Remainder(n2bit_mod2_3_remainder));  // open: quotient
  _2bit_mod2 u_2bit_mod2_4 (
    .dividee({n2bit_mod2_3_remainder, A[3]}), .divider(B), .Remainder(low_half));  // open: quotient
  _2bit_mod2 u_2bit_mod2_5 (
    .dividee({n2bit_mod2_2_remainder, A[0]}), .divider(B), .Remainder(n2bit_mod2_5_remainder));  // open: quotient
  _2bit_mod2 u_2bit_mod2_6 (
    .dividee({n2bit_mod2_5_remainder, 1'b0}), .divider(B), .Remainder(n2bit_mod2_6_remainder));  // open: quotient
  _2bit_mod2 u_2bit_mod2_7 (
    .dividee({n2bit_mod2_6_remainder, 1'b0}), .divider(B), .Remainder(n2bit_mod2_7_remainder));  // open: quotient
  _2bit_mod2 u_2bit_mod2_8 (
    .dividee({n2bit_mod2_7_remainder, 1'b0}), .divider(B), .Remainder(out_3[2:0]));  // open: quotient

  assign out_3[10:3] = A;

  // Other names for the same wires on the sheet: low_half[0] = A[2]
endmodule
