// Logisim project P0_L0_FSM.circ as structural Verilog: 3 circuits, main circuit fsm
module fsm (
  input  in_1,
  input  [1:0] in_2,
  output out_3
);

  wire clock_1_out, register_2_q, To_solve_the_problem_of_negedge_of_CLR_out;
  wire [1:0] nsl_1_next_state, register_1_q;

  NSL nsl_1 (.State(register_1_q), .Input(in_2), .Next_State(nsl_1_next_state));
  // Probe on nsl_1_next_state
  // Probe on register_1_q
  Register #(.width(2)) register_1 (
    .D(nsl_1_next_state), .Q(register_1_q), .clk(clock_1_out),
    .clr(To_solve_the_problem_of_negedge_of_CLR_out));  // open: en
  Clock clock_1 (.out(clock_1_out));
  Register #(.width(1)) register_2 (.D(in_1), .Q(register_2_q), .clk(clock_1_out));  // open: en, clr
  Output_Logic output_logic_1 (.State(register_1_q), .Input(in_2), .Output(out_3));
  and To_solve_the_problem_of_negedge_of_CLR (To_solve_the_problem_of_negedge_of_CLR_out, register_2_q, in_1);
endmodule

module NSL (
  input  [1:0] State,
  input  [1:0] Input,
  output [1:0] Next_State
);

  wire and_1_out, and_2_out, and_3_out, and_4_out, clock_1_out, counter_1_q, not_1_out, not_2_out, not_3_out,
       not_4_out, not_5_out, not_6_out, not_7_out;
  wire [1:0] multiplexer_1_out;

  Counter #(.width(1), .max('h1), .ongoal("stay")) counter_1 (
    .D(1'b0), .Q(counter_1_q), .clk(clock_1_out));  // open: load, count, carry, clr
  Clock clock_1 (.out(clock_1_out));
  Multiplexer #(.width(2)) multiplexer_1 (
    .in0(2'b00), .in1(Input), .out(multiplexer_1_out), .sel(counter_1_q));  // open: en
  not not_1 (not_1_out, State[1]);
  not not_2 (not_2_out, multiplexer_1_out[0]);
  not not_3 (not_3_out, State[0]);
  not not_4 (not_4_out, multiplexer_1_out[0]);
  not not_5 (not_5_out, multiplexer_1_out[1]);
  not not_6 (not_6_out, State[0]);
  not not_7 (not_7_out, multiplexer_1_out[0]);
  and and_1 (and_1_out, not_1_out, State[0], not_2_out);
  and and_2 (and_2_out, State[1], not_3_out, not_4_out);
  and and_3 (and_3_out, not_5_out, multiplexer_1_out[0]);
  and and_4 (and_4_out, State[1], not_6_out, not_7_out);
  or or_1 (Next_State[1], and_1_out, and_2_out);
  or or_2 (Next_State[0], and_3_out, and_4_out);
endmodule

module Output_Logic (
  input  [1:0] State,
  input  [1:0] Input,
  output Output
);

  wire not_1_out, not_2_out;

  not not_1 (not_1_out, State[0]);
  not not_2 (not_2_out, Input[0]);
  and and_1 (Output, State[1], not_1_out, not_2_out);
endmodule
