// Logisim project P0_L0_FSM_2.circ as structural Verilog: 3 circuits, main circuit fsm
module fsm (
  input  in_1,
  input  [1:0] Input,
  output out_3
);

  wire clock_1_out;
  wire [1:0] multiplexer_1_out, nsl_1_next_state, register_1_q;

  NSL nsl_1 (.State(register_1_q), .Input(Input), .Next_State(nsl_1_next_state));
  Multiplexer #(.width(2)) multiplexer_1 (
    .in0(nsl_1_next_state), .in1(2'b00), .out(multiplexer_1_out), .sel(in_1));  // open: en
  // Probe on multiplexer_1_out
  // Probe on register_1_q
  Register #(.width(2)) register_1 (.D(multiplexer_1_out), .Q(register_1_q), .clk(clock_1_out));  // open: en, clr
  Clock clock_1 (.out(clock_1_out));
  Output_Logic output_logic_1 (.State(register_1_q), .Input(Input), .Output(out_3));

  // Other names for the same wires on the sheet: reset = in_1

  // Notes on the sheet:
  //   Input: No Multiplexer!!! It makes no sense at all!!!
  //   Multiplexer can be the solution to synchronously resetable flip-flop
endmodule

module NSL (
  input  [1:0] State,
  input  [1:0] Input,
  output [1:0] Next_State
);

  wire and_1_out, and_2_out, and_3_out, and_4_out, not_1_out, not_2_out, not_3_out, not_4_out, not_5_out,
       not_6_out, not_7_out;

  not not_1 (not_1_out, State[1]);
  not not_2 (not_2_out, Input[0]);
  not not_3 (not_3_out, State[0]);
  not not_4 (not_4_out, Input[0]);
  not not_5 (not_5_out, Input[1]);
  not not_6 (not_6_out, State[0]);
  not not_7 (not_7_out, Input[0]);
  and and_1 (and_1_out, not_1_out, State[0], not_2_out);
  and and_2 (and_2_out, State[1], not_3_out, not_4_out);
  and and_3 (and_3_out, not_5_out, Input[0]);
  and and_4 (and_4_out, State[1], not_6_out, not_7_out);
  or or_1 (Next_State[1], and_1_out, and_2_out);
  or or_2 (Next_State[0], and_3_out, and_4_out);
endmodule

module Output_Logic (
  input  [1:0] State,
  input  [1:0] Input,
  output Output
);

  wire not_1_out, not_2_out;

  not not_1 (not_1_out, State[0]);
  not not_2 (not_2_out, Input[0]);
  and and_1 (Output, State[1], not_1_out, not_2_out);
endmodule
