// Logisim project P0_L0_FSM_3.circ as structural Verilog: 3 circuits, main circuit fsm
module fsm (
  input  in_1,
  input  [1:0] Input,
  output out_3
);

  wire clk, reset;
  wire [1:0] nsl_1_next_state, register_1_q;

  Clock clock_1 (.out(clk));
  Counter #(.width(1), .max('h1), .ongoal("stay")) counter_1 (
    .D(in_1), .Q(reset), .clk(clk), .clr(reset));  // open: load, count, carry
  NSL nsl_1 (.State(register_1_q), .Input(Input), .Next_State(nsl_1_next_state));
  // Probe on nsl_1_next_state
  // Probe on register_1_q
  Register #(.width(2)) register_1 (.D(nsl_1_next_state), .Q(register_1_q), .clk(clk), .clr(reset));  // open: en
  Output_Logic output_logic_1 (.State(register_1_q), .Input(Input), .Output(out_3));
endmodule

module NSL (
  input  [1:0] State,
  input  [1:0] Input,
  output [1:0] Next_State
);

  wire and_1_out, and_2_out, and_3_out, and_4_out, not_1_out, not_2_out, not_3_out, not_4_out, not_5_out,
       not_6_out, not_7_out;

  not not_1 (not_1_out, State[1]);
  not not_2 (not_2_out, Input[0]);
  not not_3 (not_3_out, State[0]);
  not not_4 (not_4_out, Input[0]);
  not not_5 (not_5_out, Input[1]);
  not not_6 (not_6_out, State[0]);
  not not_7 (not_7_out, Input[0]);
  and and_1 (and_1_out, not_1_out, State[0], not_2_out);
  and and_2 (and_2_out, State[1], not_3_out, not_4_out);
  and and_3 (and_3_out, not_5_out, Input[0]);
  and and_4 (and_4_out, State[1], not_6_out, not_7_out);
  or or_1 (Next_State[1], and_1_out, and_2_out);
  or or_2 (Next_State[0], and_3_out, and_4_out);
endmodule

module Output_Logic (
  input  [1:0] State,
  input  [1:0] Input,
  output Output
);

  wire not_1_out, not_2_out;

  not not_1 (not_1_out, State[0]);
  not not_2 (not_2_out, Input[0]);
  and and_1 (Output, State[1], not_1_out, not_2_out);
endmodule
