// Logisim project P0_L0_GRF.circ as structural Verilog: 1 circuit, main circuit grf
module grf (
  input  CLK,
  input  Reset,
  input  WE,
  input  [4:0] A1,
  input  [4:0] A2,
  input  [4:0] A3,
  input  [31:0] WD,
  output [31:0] RD1,
  output [31:0] RD2
);

  wire enw0, enw1, enw2, enw3, enw4, enw5, enw6, enw7, enw8, enw9, enw10, enw11, enw12, enw13, enw14, enw15,
       enw16, enw17, enw18, enw19, enw20, enw21, enw22, enw23, enw24, enw25, enw26, enw27, enw28, enw29,
       enw30, enw31;
  wire [31:0] r0, r1, r2, r3, r4, r5, r6, r7, r8, r9, r10, r11, r12, r13, r14, r15, r16, r17, r18, r19, r20,
       r21, r22, r23, r24, r25, r26, r27, r28, r29, r30, r31;

  Decoder #(.select(5), .disabled(0)) decoder_1 (
    .out0(enw0), .out1(enw1), .out2(enw2), .out3(enw3), .out4(enw4), .out5(enw5), .out6(enw6), .out7(enw7),
    .out8(enw8), .out9(enw9), .out10(enw10), .out11(enw11), .out12(enw12), .out13(enw13), .out14(enw14),
    .out15(enw15), .out16(enw16), .out17(enw17), .out18(enw18), .out19(enw19), .out20(enw20), .out21(enw21),
    .out22(enw22), .out23(enw23), .out24(enw24), .out25(enw25), .out26(enw26), .out27(enw27), .out28(enw28),
    .out29(enw29), .out30(enw30), .out31(enw31), .sel(A3), .en(WE));
  Register #(.width(32)) register_1 (.D(WD), .en(enw0), .Q(r0), .clk(CLK), .clr(1'b1));
  Register #(.width(32)) register_2 (.D(WD), .en(enw16), .Q(r16), .clk(CLK), .clr(Reset));
  Register #(.width(32)) register_3 (.D(WD), .en(enw1), .Q(r1), .clk(CLK), .clr(Reset));
  Register #(.width(32)) register_4 (.D(WD), .en(enw17), .Q(r17), .clk(CLK), .clr(Reset));
  Register #(.width(32)) register_5 (.D(WD), .en(enw2), .Q(r2), .clk(CLK), .clr(Reset));
  Register #(.width(32)) register_6 (.D(WD), .en(enw18), .Q(r18), .clk(CLK), .clr(Reset));
  Register #(.width(32)) register_7 (.D(WD), .en(enw3), .Q(r3), .clk(CLK), .clr(Reset));
  Register #(.width(32)) register_8 (.D(WD), .en(enw19), .Q(r19), .clk(CLK), .clr(Reset));
  Register #(.width(32)) register_9 (.D(WD), .en(enw4), .Q(r4), .clk(CLK), .clr(Reset));
  Register #(.width(32)) register_10 (.D(WD), .en(enw20), .Q(r20), .clk(CLK), .clr(Reset));
  Register #(.width(32)) register_11 (.D(WD), .en(enw5), .Q(r5), .clk(CLK), .clr(Reset));
  Register #(.width(32)) register_12 (.D(WD), .en(enw21), .Q(r21), .clk(CLK), .clr(Reset));
  Register #(.width(32)) register_13 (.D(WD), .en(enw6), .Q(r6), .clk(CLK), .clr(Reset));
  Register #(.width(32)) register_14 (.D(WD), .en(enw22), .Q(r22), .clk(CLK), .clr(Reset));
  Register #(.width(32)) register_15 (.D(WD), .en(enw7), .Q(r7), .clk(CLK), .clr(Reset));
  Register #(.width(32)) register_16 (.D(WD), .en(enw23), .Q(r23), .clk(CLK), .clr(Reset));
  Register #(.width(32)) register_17 (.D(WD), .en(enw8), .Q(r8), .clk(CLK), .clr(Reset));
  Register #(.width(32)) register_18 (.D(WD), .en(enw24), .Q(r24), .clk(CLK), .clr(Reset));
  Register #(.width(32)) register_19 (.D(WD), .en(enw9), .Q(r9), .clk(CLK), .clr(Reset));
  Register #(.width(32)) register_20 (.D(WD), .en(enw25), .Q(r25), .clk(CLK), .clr(Reset));
  Register #(.width(32)) register_21 (.D(WD), .en(enw10), .Q(r10), .clk(CLK), .clr(Reset));
  Register #(.width(32)) register_22 (.D(WD), .en(enw26), .Q(r26), .clk(CLK), .clr(Reset));
  Register #(.width(32)) register_23 (.D(WD), .en(enw11), .Q(r11), .clk(CLK), .clr(Reset));
  Register #(.width(32)) register_24 (.D(WD), .en(enw27), .Q(r27), .clk(CLK), .clr(Reset));
  Register #(.width(32)) register_25 (.D(WD), .en(enw12), .Q(r12), .clk(CLK), .clr(Reset));
  Register #(.width(32)) register_26 (.D(WD), .en(enw28), .Q(r28), .clk(CLK), .clr(Reset));
  Register #(.width(32)) register_27 (.D(WD), .en(enw13), .Q(r13), .clk(CLK), .clr(Reset));
  Register #(.width(32)) register_28 (.D(WD), .en(enw29), .Q(r29), .clk(CLK), .clr(Reset));
  Register #(.width(32)) register_29 (.D(WD), .en(enw14), .Q(r14), .clk(CLK), .clr(Reset));
  Register #(.width(32)) register_30 (.D(WD), .en(enw30), .Q(r30), .clk(CLK), .clr(Reset));
  Register #(.width(32)) register_31 (.D(WD), .en(enw15), .Q(r15), .clk(CLK), .clr(Reset));
  Register #(.width(32)) register_32 (.D(WD), .en(enw31), .Q(r31), .clk(CLK), .clr(Reset));
  Multiplexer #(.select(5), .width(32)) multiplexer_1 (
    .in0(r0), .in1(r1), .in2(r2), .in3(r3), .in4(r4), .in5(r5), .in6(r6), .in7(r7), .in8(r8), .in9(r9),
    .in10(r10), .in11(r11), .in12(r12), .in13(r13), .in14(r14), .in15(r15), .in16(r16), .in17(r17),
    .in18(r18), .in19(r19), .in20(r20), .in21(r21), .in22(r22), .in23(r23), .in24(r24), .in25(r25),
    .in26(r26), .in27(r27), .in28(r28), .in29(r29), .in30(r30), .in31(r31), .out(RD1), .sel(A1));  // open: en
  Multiplexer #(.select(5), .width(32)) multiplexer_2 (
    .in0(r0), .in1(r1), .in2(r2), .in3(r3), .in4(r4), .in5(r5), .in6(r6), .in7(r7), .in8(r8), .in9(r9),
    .in10(r10), .in11(r11), .in12(r12), .in13(r13), .in14(r14), .in15(r15), .in16(r16), .in17(r17),
    .in18(r18), .in19(r19), .in20(r20), .in21(r21), .in22(r22), .in23(r23), .in24(r24), .in25(r25),
    .in26(r26), .in27(r27), .in28(r28), .in29(r29), .in30(r30), .in31(r31), .out(RD2), .sel(A2));  // open: en

  // Notes on the sheet:
  //   Disabled Output: 0
endmodule
