// Logisim project P0_L1_ftoi.circ as structural Verilog: 3 circuits, main circuit ftoi
module ftoi (
  input  [15:0] in_1,
  output [31:0] out_2
);

  wire and_1_out, and_2_out, comparator_1_lt, or_1_out;
  wire [31:0] normalized_2_1_out_2;

  and and_1 (and_1_out, in_1[10], in_1[11], in_1[12], in_1[13], in_1[14]);
  and and_2 (and_2_out, ~in_1[10], ~in_1[11], ~in_1[12], ~in_1[13], ~in_1[14]);  // AND_Gate
  Comparator #(.width(5), .mode("unsigned")) comparator_1 (
    .a(in_1[14:10]), .b(5'b01111), .lt(comparator_1_lt));  // open: gt, eq
  or or_1 (or_1_out, comparator_1_lt, and_1_out, and_2_out);
  Normalized_2 normalized_2_1 (.in_1(in_1), .out_2(normalized_2_1_out_2));
  Multiplexer #(.width(32)) multiplexer_1 (
    .in0(normalized_2_1_out_2), .in1({32{1'b0}}), .out(out_2), .sel(or_1_out));  // open: en

  // Other names for the same wires on the sheet: floating[15:0] = in_1; int[31:0] = out_2
endmodule

module Normalized (
  input  [15:0] in_1,
  output [31:0] out_2
);

  wire [0:0] not_1_out;
  wire [1:1] and_1_out;
  wire [2:2] and_2_out;
  wire [3:3] and_3_out;
  wire [31:0] adder_1_out, bit_extender_1_out, not_2_out, shifter_1_out, shifter_2_out, shifter_3_out,
       shifter_4_out, shifter_5_out;

  // Probe on {1'b1, in_1[9:0]}
  // Probe on bit_extender_1_out
  assign bit_extender_1_out = {{21{1'b0}}, {1'b1, in_1[9:0]}};  // Bit_Extender bit_extender_1
  and and_1 (and_1_out[1], in_1[11], 1'b1);
  and and_2 (and_2_out[2], in_1[12], 1'b1);
  and and_3 (and_3_out[3], in_1[13], 1'b1);
  not not_1 (not_1_out[0], in_1[10]);
  // Probe on {3'b000, and_1_out[1], 1'b0}
  // Probe on shifter_1_out
  Shifter #(.width(32)) shifter_1 (.in(bit_extender_1_out), .\dist ({3'b000, and_1_out[1], 1'b0}), .out(shifter_1_out));
  // Probe on {2'b00, and_2_out[2], 2'b00}
  // Probe on shifter_2_out
  Shifter #(.width(32)) shifter_2 (.in(shifter_1_out), .\dist ({2'b00, and_2_out[2], 2'b00}), .out(shifter_2_out));
  // Probe on {1'b0, and_3_out[3], 3'b000}
  Shifter #(.width(32)) shifter_3 (.in(shifter_2_out), .\dist ({1'b0, and_3_out[3], 3'b000}), .out(shifter_3_out));
  // Probe on {4'b0000, not_1_out[0]}
  // Probe on shifter_3_out
  Shifter #(.width(32)) shifter_4 (.in(shifter_3_out), .\dist ({4'b0000, not_1_out[0]}), .out(shifter_4_out));
  // Probe on shifter_4_out
  Shifter #(.width(32), .shift("ar")) shifter_5 (.in(shifter_4_out), .\dist (5'b01010), .out(shifter_5_out));
  assign not_2_out = ~shifter_5_out;  // NOT_Gate not_2, 32 bits wide
  Adder #(.width(32)) adder_1 (.a(not_2_out), .b(32'h1), .out(adder_1_out));  // open: cin, cout
  // Probe on shifter_5_out
  Multiplexer #(.width(32)) multiplexer_1 (
    .in0(shifter_5_out), .in1(adder_1_out), .out(out_2), .sel(in_1[15]));  // open: en

  // Other names for the same wires on the sheet: power0 = in_1[10]; power1 = in_1[11]; power2 = in_1[12];
  //   power3 = in_1[13]; symbol = in_1[15]
endmodule

module Normalized_2 (
  input  [15:0] in_1,
  output [31:0] out_2
);

  wire [4:0] subtractor_1_out;
  wire [31:0] adder_1_out, bit_extender_1_out, not_1_out, shifter_1_out, shifter_2_out;

  // Probe on {1'b1, in_1[9:0]}
  // Probe on bit_extender_1_out
  assign bit_extender_1_out = {{21{1'b0}}, {1'b1, in_1[9:0]}};  // Bit_Extender bit_extender_1
  Subtractor #(.width(5)) subtractor_1 (.a(in_1[14:10]), .b(5'b01111), .out(subtractor_1_out));  // open: bin, bout
  Shifter #(.width(32)) shifter_1 (.in(bit_extender_1_out), .\dist (subtractor_1_out), .out(shifter_1_out));
  Shifter #(.width(32), .shift("ar")) shifter_2 (.in(shifter_1_out), .\dist (5'b01010), .out(shifter_2_out));
  assign not_1_out = ~shifter_2_out;  // NOT_Gate not_1, 32 bits wide
  Adder #(.width(32)) adder_1 (.a(not_1_out), .b(32'h1), .out(adder_1_out));  // open: cin, cout
  // Probe on shifter_2_out
  Multiplexer #(.width(32)) multiplexer_1 (
    .in0(shifter_2_out), .in1(adder_1_out), .out(out_2), .sel(in_1[15]));  // open: en

  // Other names for the same wires on the sheet: symbol = in_1[15]
endmodule
