// Logisim project P0_L1_navigation_2020.circ as structural Verilog: 3 circuits, main circuit navigation
module navigation (
  input  [1:0] dir,
  input  clk,
  input  reset,
  output out_4,
  output out_5
);

  wire [8:0] nsl_1_next_state, register_1_q;

  // Probe on dir
  NSL nsl_1 (.status(register_1_q), .dir(dir), .clk(clk), .reset(reset), .next_state(nsl_1_next_state));
  // Probe on nsl_1_next_state
  // Probe on nsl_1_next_state
  Register #(.width(9)) register_1 (.D(nsl_1_next_state), .Q(register_1_q), .clk(clk), .clr(reset));  // open: en
  // Probe on register_1_q
  Output_Logic output_logic_1 (.status(register_1_q), .arrive(out_4), .hit(out_5));

  // Other names for the same wires on the sheet: arrive = out_4; hit = out_5

  // Notes on the sheet:
  //   BUG!!!!!
endmodule

module NSL (
  input  [8:0] status,
  input  [1:0] dir,
  input  clk,
  input  reset,
  output [8:0] next_state
);

  wire and_1_out, and_2_out, and_3_out, and_4_out, and_5_out, and_6_out, and_10_out, and_11_out, and_12_out,
       and_13_out, and_14_out, and_15_out, counter_1_q, not_1_out, not_2_out, not_3_out, not_4_out,
       not_5_out, not_6_out, not_7_out, not_8_out, not_9_out, not_10_out, not_11_out, not_12_out, not_13_out,
       not_14_out, not_15_out, not_16_out, not_17_out, not_18_out, not_19_out, not_20_out, not_21_out,
       not_22_out, not_23_out, not_24_out, not_25_out, not_26_out, not_27_out, not_28_out, not_29_out,
       not_30_out, not_31_out, not_32_out, not_33_out, not_34_out, not_35_out, not_36_out, not_37_out,
       not_38_out, not_39_out, not_40_out, not_41_out, not_42_out, not_43_out, not_44_out, not_45_out,
       not_46_out, not_47_out, not_48_out, not_49_out, not_50_out, not_51_out, not_52_out, not_53_out,
       not_54_out, not_55_out, not_56_out, not_57_out, not_58_out, not_59_out, not_60_out, not_61_out,
       not_62_out, not_63_out, not_64_out, not_65_out, not_66_out, not_67_out, not_68_out, not_69_out,
       not_70_out, not_71_out, not_72_out, not_73_out, not_74_out, not_75_out, not_76_out, not_77_out,
       not_78_out, not_79_out, not_80_out, not_81_out, not_82_out, not_83_out, not_84_out, not_85_out,
       not_86_out, not_87_out, not_88_out, not_89_out, not_90_out, not_91_out, not_92_out, not_93_out,
       not_94_out, not_95_out, not_96_out, not_97_out, not_98_out, not_99_out, not_100_out, not_101_out,
       not_102_out, not_103_out, not_104_out, not_105_out, not_106_out, not_107_out, not_108_out,
       not_109_out, not_110_out, not_111_out, not_112_out, not_113_out, not_114_out, not_115_out,
       not_116_out, not_117_out, not_118_out;
  wire [8:0] multiplexer_1_out;

  Counter #(.width(1), .max('h1), .ongoal("stay")) counter_1 (
    .D(1'b0), .Q(counter_1_q), .clk(clk), .clr(reset));  // open: load, count, carry
  Multiplexer #(.width(9)) multiplexer_1 (
    .in0(9'h1), .in1(status), .out(multiplexer_1_out), .sel(counter_1_q));  // open: en
  not not_1 (not_1_out, multiplexer_1_out[0]);
  not not_2 (not_2_out, multiplexer_1_out[1]);
  not not_3 (not_3_out, multiplexer_1_out[2]);
  not not_4 (not_4_out, multiplexer_1_out[3]);
  not not_5 (not_5_out, multiplexer_1_out[4]);
  not not_6 (not_6_out, multiplexer_1_out[6]);
  not not_7 (not_7_out, multiplexer_1_out[7]);
  not not_8 (not_8_out, dir[1]);
  not not_9 (not_9_out, multiplexer_1_out[0]);
  not not_10 (not_10_out, multiplexer_1_out[1]);
  not not_11 (not_11_out, multiplexer_1_out[2]);
  not not_12 (not_12_out, multiplexer_1_out[3]);
  not not_13 (not_13_out, multiplexer_1_out[4]);
  not not_14 (not_14_out, multiplexer_1_out[6]);
  not not_15 (not_15_out, multiplexer_1_out[7]);
  not not_16 (not_16_out, dir[0]);
  not not_17 (not_17_out, multiplexer_1_out[0]);
  not not_18 (not_18_out, multiplexer_1_out[1]);
  not not_19 (not_19_out, multiplexer_1_out[2]);
  not not_20 (not_20_out, multiplexer_1_out[3]);
  not not_21 (not_21_out, multiplexer_1_out[4]);
  not not_22 (not_22_out, multiplexer_1_out[6]);
  not not_23 (not_23_out, multiplexer_1_out[7]);
  not not_24 (not_24_out, dir[1]);
  not not_25 (not_25_out, dir[0]);
  not not_26 (not_26_out, multiplexer_1_out[0]);
  not not_27 (not_27_out, multiplexer_1_out[1]);
  not not_28 (not_28_out, multiplexer_1_out[2]);
  not not_29 (not_29_out, multiplexer_1_out[3]);
  not not_30 (not_30_out, multiplexer_1_out[5]);
  not not_31 (not_31_out, multiplexer_1_out[7]);
  not not_32 (not_32_out, multiplexer_1_out[8]);
  not not_33 (not_33_out, dir[1]);
  not not_34 (not_34_out, multiplexer_1_out[0]);
  not not_35 (not_35_out, multiplexer_1_out[1]);
  not not_36 (not_36_out, multiplexer_1_out[2]);
  not not_37 (not_37_out, multiplexer_1_out[3]);
  not not_38 (not_38_out, multiplexer_1_out[5]);
  not not_39 (not_39_out, multiplexer_1_out[7]);
  not not_40 (not_40_out, multiplexer_1_out[8]);
  not not_41 (not_41_out, dir[1]);
  not not_42 (not_42_out, dir[0]);
  not not_43 (not_43_out, multiplexer_1_out[0]);
  not not_44 (not_44_out, multiplexer_1_out[1]);
  not not_45 (not_45_out, multiplexer_1_out[2]);
  not not_46 (not_46_out, multiplexer_1_out[3]);
  not not_47 (not_47_out, multiplexer_1_out[5]);
  not not_48 (not_48_out, multiplexer_1_out[7]);
  not not_49 (not_49_out, multiplexer_1_out[8]);
  not not_50 (not_50_out, multiplexer_1_out[0]);
  not not_51 (not_51_out, multiplexer_1_out[1]);
  not not_52 (not_52_out, multiplexer_1_out[4]);
  not not_53 (not_53_out, multiplexer_1_out[5]);
  not not_54 (not_54_out, multiplexer_1_out[6]);
  not not_55 (not_55_out, multiplexer_1_out[7]);
  not not_56 (not_56_out, multiplexer_1_out[8]);
  not not_57 (not_57_out, dir[1]);
  not not_58 (not_58_out, multiplexer_1_out[0]);
  not not_59 (not_59_out, multiplexer_1_out[1]);
  not not_60 (not_60_out, multiplexer_1_out[4]);
  not not_61 (not_61_out, multiplexer_1_out[5]);
  not not_62 (not_62_out, multiplexer_1_out[6]);
  not not_63 (not_63_out, multiplexer_1_out[7]);
  not not_64 (not_64_out, multiplexer_1_out[8]);
  not not_65 (not_65_out, dir[1]);
  not not_66 (not_66_out, dir[0]);
  not not_67 (not_67_out, multiplexer_1_out[0]);
  not not_68 (not_68_out, multiplexer_1_out[1]);
  not not_69 (not_69_out, multiplexer_1_out[4]);
  not not_70 (not_70_out, multiplexer_1_out[5]);
  not not_71 (not_71_out, multiplexer_1_out[6]);
  not not_72 (not_72_out, multiplexer_1_out[7]);
  not not_73 (not_73_out, multiplexer_1_out[8]);
  not not_74 (not_74_out, multiplexer_1_out[2]);
  not not_75 (not_75_out, multiplexer_1_out[3]);
  not not_76 (not_76_out, multiplexer_1_out[4]);
  not not_77 (not_77_out, multiplexer_1_out[5]);
  not not_78 (not_78_out, multiplexer_1_out[6]);
  not not_79 (not_79_out, multiplexer_1_out[7]);
  not not_80 (not_80_out, multiplexer_1_out[8]);
  not not_81 (not_81_out, dir[1]);
  not not_82 (not_82_out, dir[0]);
  not not_83 (not_83_out, multiplexer_1_out[0]);
  not not_84 (not_84_out, multiplexer_1_out[1]);
  not not_85 (not_85_out, multiplexer_1_out[2]);
  not not_86 (not_86_out, multiplexer_1_out[3]);
  not not_87 (not_87_out, multiplexer_1_out[5]);
  not not_88 (not_88_out, multiplexer_1_out[7]);
  not not_89 (not_89_out, multiplexer_1_out[8]);
  not not_90 (not_90_out, dir[0]);
  not not_91 (not_91_out, multiplexer_1_out[0]);
  not not_92 (not_92_out, multiplexer_1_out[1]);
  not not_93 (not_93_out, multiplexer_1_out[2]);
  not not_94 (not_94_out, multiplexer_1_out[3]);
  not not_95 (not_95_out, multiplexer_1_out[4]);
  not not_96 (not_96_out, multiplexer_1_out[6]);
  not not_97 (not_97_out, multiplexer_1_out[7]);
  not not_98 (not_98_out, multiplexer_1_out[2]);
  not not_99 (not_99_out, multiplexer_1_out[3]);
  not not_100 (not_100_out, multiplexer_1_out[4]);
  not not_101 (not_101_out, multiplexer_1_out[5]);
  not not_102 (not_102_out, multiplexer_1_out[6]);
  not not_103 (not_103_out, multiplexer_1_out[7]);
  not not_104 (not_104_out, multiplexer_1_out[8]);
  not not_105 (not_105_out, multiplexer_1_out[2]);
  not not_106 (not_106_out, multiplexer_1_out[3]);
  not not_107 (not_107_out, multiplexer_1_out[4]);
  not not_108 (not_108_out, multiplexer_1_out[5]);
  not not_109 (not_109_out, multiplexer_1_out[6]);
  not not_110 (not_110_out, multiplexer_1_out[7]);
  not not_111 (not_111_out, multiplexer_1_out[8]);
  not not_112 (not_112_out, multiplexer_1_out[0]);
  not not_113 (not_113_out, multiplexer_1_out[1]);
  not not_114 (not_114_out, multiplexer_1_out[4]);
  not not_115 (not_115_out, multiplexer_1_out[5]);
  not not_116 (not_116_out, multiplexer_1_out[6]);
  not not_117 (not_117_out, multiplexer_1_out[8]);
  not not_118 (not_118_out, dir[0]);
  and and_1 (and_1_out, not_1_out, not_2_out, not_3_out, not_4_out, not_5_out, not_6_out, not_7_out, not_8_out, dir[0]);
  and and_2 (and_2_out, not_9_out, not_10_out, not_11_out, not_12_out, not_13_out, not_14_out, not_15_out, dir[1], not_16_out);
  and and_3 (and_3_out, not_17_out, not_18_out, not_19_out, not_20_out, not_21_out, not_22_out, not_23_out, not_24_out, not_25_out);
  and and_4 (and_4_out, not_26_out, not_27_out, not_28_out, not_29_out, not_30_out, not_31_out, not_32_out, not_33_out, dir[0]);
  and and_5 (and_5_out, not_34_out, not_35_out, not_36_out, not_37_out, not_38_out, not_39_out, not_40_out, not_41_out, not_42_out);
  and and_6 (and_6_out, not_43_out, not_44_out, not_45_out, not_46_out, not_47_out, not_48_out, not_49_out, dir[1], dir[0]);
  and and_7 (next_state[5], not_50_out, not_51_out, not_52_out, not_53_out, not_54_out, not_55_out, not_56_out, not_57_out, dir[0]);
  and and_8 (next_state[4], not_58_out, not_59_out, not_60_out, not_61_out, not_62_out, not_63_out, not_64_out, not_65_out, not_66_out);
  and and_9 (next_state[3], not_67_out, not_68_out, not_69_out, not_70_out, not_71_out, not_72_out, not_73_out, dir[1], dir[0]);
  and and_10 (and_10_out, not_74_out, not_75_out, not_76_out, not_77_out, not_78_out, not_79_out, not_80_out, not_81_out, not_82_out);
  and and_11 (and_11_out, not_83_out, not_84_out, not_85_out, not_86_out, not_87_out, not_88_out, not_89_out, dir[1], not_90_out);
  and and_12 (and_12_out, not_91_out, not_92_out, not_93_out, not_94_out, not_95_out, not_96_out, not_97_out, dir[1], dir[0]);
  and and_13 (and_13_out, not_98_out, not_99_out, not_100_out, not_101_out, not_102_out, not_103_out, not_104_out, dir[0]);
  and and_14 (and_14_out, not_105_out, not_106_out, not_107_out, not_108_out, not_109_out, not_110_out, not_111_out, dir[1]);
  and and_15 (and_15_out, not_112_out, not_113_out, not_114_out, not_115_out, not_116_out, not_117_out, dir[1], not_118_out);
  or or_1 (next_state[8], and_1_out, and_2_out);
  or or_2 (next_state[7], and_3_out, and_4_out);
  or or_3 (next_state[6], and_5_out, and_6_out);
  or or_4 (next_state[2], and_10_out, and_11_out, and_12_out);
  or or_5 (next_state[1], and_13_out, and_14_out);
  or or_6 (next_state[0], and_15_out, multiplexer_1_out[7]);

  // Notes on the sheet:
  //   BUG!!!!!
  //   BUG!!!!!
endmodule

module Output_Logic (
  input  [8:0] status,
  output arrive,
  output hit
);

  or or_1 (hit, status[1], status[3], status[6], status[8]);

  assign arrive = status[7];
endmodule
