// Logisim project P0_L1_navigation_2020_2.circ as structural Verilog: 4 circuits, main circuit navigation
module navigation (
  input  [1:0] dir,
  input  clk,
  input  reset,
  output out_4,
  output out_5
);

  wire counter_1_q, nsl_1_state0_, nsl_1_state1_, nsl_1_state2_, outputlogic_1_hit, state_register_1_out_6,
       state_register_1_out_7, state_register_1_out_8, state_register_2_out_6, state_register_2_out_7,
       state_register_2_out_8;

  NSL nsl_1 (
    .state2(state_register_1_out_6), .state1(state_register_1_out_7), .state0(state_register_1_out_8),
    .in1(dir[1]), .in0(dir[0]), .state2_(nsl_1_state2_), .state1_(nsl_1_state1_), .state0_(nsl_1_state0_));
  State_Register state_register_1 (
    .in_1(nsl_1_state2_), .in_2(nsl_1_state1_), .in_3(nsl_1_state0_), .CLK(clk), .Reset(reset),
    .out_6(state_register_1_out_6), .out_7(state_register_1_out_7), .out_8(state_register_1_out_8));
  State_Register state_register_2 (
    .in_1(state_register_1_out_6), .in_2(state_register_1_out_7), .in_3(state_register_1_out_8), .CLK(clk),
    .Reset(reset), .out_6(state_register_2_out_6), .out_7(state_register_2_out_7),
    .out_8(state_register_2_out_8));
  OutputLogic outputlogic_1 (
    .state2(state_register_1_out_6), .state1(state_register_1_out_7), .state0(state_register_1_out_8),
    .pre2(state_register_2_out_6), .pre1(state_register_2_out_7), .pre0(state_register_2_out_8),
    .hit(outputlogic_1_hit), .arrive(out_4));
  Counter #(.width(1), .max('h1), .ongoal("stay")) counter_1 (
    .Q(counter_1_q), .clk(clk), .clr(reset));  // open: load, D, count, carry
  Multiplexer multiplexer_1 (.in0(1'b0), .in1(outputlogic_1_hit), .out(out_5), .sel(counter_1_q));  // open: en

  // Other names for the same wires on the sheet: arrive = out_4; hit = out_5
endmodule

module NSL (
  input  state2,
  input  state1,
  input  state0,
  input  in1,
  input  in0,
  output state2_,
  output state1_,
  output state0_
);

  wire and_1_out, and_2_out, and_3_out, and_4_out, and_5_out, and_6_out, and_7_out, and_8_out, and_9_out,
       and_10_out, and_11_out, not_1_out, not_2_out, not_3_out, not_4_out, not_5_out, not_6_out, not_7_out,
       not_8_out, not_9_out, not_10_out, not_11_out, not_12_out, not_13_out, not_14_out, not_15_out,
       not_16_out, not_17_out;

  not not_1 (not_1_out, state0);
  not not_2 (not_2_out, in1);
  not not_3 (not_3_out, in0);
  not not_4 (not_4_out, in1);
  not not_5 (not_5_out, state1);
  not not_6 (not_6_out, in1);
  not not_7 (not_7_out, in1);
  not not_8 (not_8_out, in0);
  not not_9 (not_9_out, state0);
  not not_10 (not_10_out, in1);
  not not_11 (not_11_out, state0);
  not not_12 (not_12_out, in0);
  not not_13 (not_13_out, state2);
  not not_14 (not_14_out, state1);
  not not_15 (not_15_out, in1);
  not not_16 (not_16_out, in0);
  not not_17 (not_17_out, in0);
  and and_1 (and_1_out, state1, not_1_out, not_2_out, not_3_out);
  and and_2 (and_2_out, state1, state0, not_4_out, in0);
  and and_3 (and_3_out, not_5_out, state0, not_6_out);
  and and_4 (and_4_out, state0, not_7_out, not_8_out);
  and and_5 (and_5_out, state1, not_9_out, not_10_out, in0);
  and and_6 (and_6_out, state1, not_11_out, in1, not_12_out);
  and and_7 (and_7_out, state1, state0, in1, in0);
  and and_8 (and_8_out, not_13_out, not_14_out, not_15_out, not_16_out);
  and and_9 (and_9_out, state0, in1, in0);
  and and_10 (and_10_out, state1, in1, in0);
  and and_11 (and_11_out, state1, state0, not_17_out);
  or or_1 (state2_, and_1_out, and_2_out);
  or or_2 (state1_, and_3_out, and_4_out, and_5_out, and_6_out, and_7_out);
  or or_3 (state0_, and_8_out, and_9_out, and_10_out, and_11_out);
endmodule

module OutputLogic (
  input  state2,
  input  state1,
  input  state0,
  input  pre2,
  input  pre1,
  input  pre0,
  output hit,
  output arrive
);

  wire and_1_out, and_2_out, and_3_out, and_4_out, not_1_out, not_2_out, not_3_out, not_4_out, not_5_out,
       not_6_out, not_7_out, not_8_out, not_9_out, not_10_out, not_11_out, not_12_out, not_13_out,
       not_14_out, not_15_out;

  not not_1 (not_1_out, state2);
  not not_2 (not_2_out, state1);
  not not_3 (not_3_out, state0);
  not not_4 (not_4_out, pre2);
  not not_5 (not_5_out, pre1);
  not not_6 (not_6_out, pre0);
  not not_7 (not_7_out, state1);
  not not_8 (not_8_out, pre2);
  not not_9 (not_9_out, pre1);
  not not_10 (not_10_out, state0);
  not not_11 (not_11_out, pre2);
  not not_12 (not_12_out, pre0);
  not not_13 (not_13_out, pre2);
  not not_14 (not_14_out, state1);
  not not_15 (not_15_out, state0);
  and and_1 (and_1_out, not_1_out, not_2_out, not_3_out, not_4_out, not_5_out, not_6_out);
  and and_2 (and_2_out, not_7_out, state0, not_8_out, not_9_out, pre0);
  and and_3 (and_3_out, state1, not_10_out, not_11_out, pre1, not_12_out);
  and and_4 (and_4_out, state1, state0, not_13_out, pre1, pre0);
  and and_5 (arrive, state2, not_14_out, not_15_out);
  or or_1 (hit, and_1_out, and_2_out, and_3_out, and_4_out);
endmodule

module State_Register (
  input  in_1,
  input  in_2,
  input  in_3,
  input  CLK,
  input  Reset,
  output out_6,
  output out_7,
  output out_8
);

  Register #(.width(1)) register_1 (.D(in_1), .Q(out_6), .clk(CLK), .clr(Reset));  // open: en
  Register #(.width(1)) register_2 (.D(in_2), .Q(out_7), .clk(CLK), .clr(Reset));  // open: en
  Register #(.width(1)) register_3 (.D(in_3), .Q(out_8), .clk(CLK), .clr(Reset));  // open: en
endmodule
