// Logisim project P0_L1_navigation_2020_XSP.circ as structural Verilog
module navigation (
  input  [1:0] dir,
  input  clk,
  input  rst,
  output arrive,
  output hit
);

  wire and_1_out, arrve_1_arrive, comparator_1_eq, not_1_out;
  wire [1:0] Statue_q, trans_1_s_prime;

  trans trans_1 (.dir(dir), .s(Statue_q), .arrive(arrive), .s_prime(trans_1_s_prime));
  arrve arrve_1 (.dir(dir), .s(Statue_q), .a(arrive), .arrive(arrve_1_arrive));
  Comparator #(.width(2)) comparator_1 (.a(trans_1_s_prime), .b(Statue_q), .eq(comparator_1_eq));  // open: gt, lt
  not not_1 (not_1_out, arrive);
  and and_1 (and_1_out, not_1_out, comparator_1_eq);
  Register #(.width(2)) Statue (.D(trans_1_s_prime), .Q(Statue_q), .clk(clk), .clr(rst));  // open: en
  Register #(.width(1)) u_Arrive (.D(arrve_1_arrive), .Q(arrive), .clk(clk), .clr(rst));  // open: en
  Register #(.width(1)) u_Hit (.D(and_1_out), .Q(hit), .clk(clk), .clr(rst));  // open: en
endmodule

module trans (
  input  [1:0] dir,
  input  [1:0] s,
  input  arrive,
  output [1:0] s_prime
);

  wire and_1_out, and_2_out, and_3_out, and_4_out, and_5_out, and_6_out, and_7_out, and_8_out, not_1_out,
       not_2_out, not_3_out, not_4_out;
  wire [1:0] or_2_out;

  not not_1 (not_1_out, s[1]);
  not not_2 (not_2_out, dir[0]);
  not not_3 (not_3_out, dir[1]);
  not not_4 (not_4_out, s[0]);
  and and_1 (and_1_out, not_1_out, s[0], not_3_out);
  and and_2 (and_2_out, s[0], not_3_out, dir[0]);
  and and_3 (and_3_out, s[1], not_4_out, not_3_out, not_2_out);
  and and_4 (and_4_out, s[1], not_4_out, dir[1], dir[0]);
  and and_5 (and_5_out, s[1], s[0], dir[1], not_2_out);
  and and_6 (and_6_out, s[1], dir[1], not_2_out);
  and and_7 (and_7_out, s[0], dir[0]);
  and and_8 (and_8_out, not_1_out, not_4_out, not_3_out, not_2_out);
  or or_1 (or_2_out[1], and_1_out, and_2_out, and_3_out, and_4_out, and_5_out);
  or or_2 (or_2_out[0], and_6_out, and_7_out, and_8_out);
  Multiplexer #(.width(2)) multiplexer_1 (.in0(or_2_out), .in1(2'b00), .out(s_prime), .sel(arrive));  // open: en
endmodule

module arrve (
  input  [1:0] dir,
  input  [1:0] s,
  input  a,
  output arrive
);

  wire and_1_out, and_2_out, not_1_out, not_2_out, not_3_out, not_4_out, not_5_out, not_6_out;

  not not_1 (not_1_out, a);
  not not_2 (not_2_out, s[0]);
  not not_3 (not_3_out, dir[1]);
  not not_4 (not_4_out, a);
  not not_5 (not_5_out, dir[1]);
  not not_6 (not_6_out, dir[0]);
  and and_1 (and_1_out, not_1_out, s[1], not_2_out, not_3_out, dir[0]);
  and and_2 (and_2_out, not_4_out, s[1], s[0], not_5_out, not_6_out);
  or or_1 (arrive, and_1_out, and_2_out);
endmodule
