// Logisim project 1.circ as structural Verilog: 4 circuits, main circuit main
module main (
  input  [1:0] Team_Leader,
  input  [1:0] Mem1,
  input  [1:0] Mem2,
  input  [1:0] Mem3,
  output out_5
);

  wire comparator_1_gt, leader_1_out_5;
  wire [2:0] adder_4_1_out_5, adder_4_2_out_5, leader_1_out_2, leader_1_out_3, member_1_out_2,
       member_1_out_3, member_2_out_2, member_2_out_3, member_3_out_2, member_3_out_3;

  Leader leader_1 (
    .Team_Leader(Team_Leader), .out_2(leader_1_out_2), .out_3(leader_1_out_3), .out_5(leader_1_out_5));  // open: out_4
  Member member_1 (.Team_Member(Mem1), .out_2(member_1_out_2), .out_3(member_1_out_3));  // open: out_4
  Member member_2 (.Team_Member(Mem2), .out_2(member_2_out_2), .out_3(member_2_out_3));  // open: out_4
  Member member_3 (.Team_Member(Mem3), .out_2(member_3_out_2), .out_3(member_3_out_3));  // open: out_4
  adder_4 adder_4_1 (
    .in_1(leader_1_out_2), .in_2(member_1_out_2), .in_3(member_2_out_2), .in_4(member_3_out_2),
    .out_5(adder_4_1_out_5));
  adder_4 adder_4_2 (
    .in_1(leader_1_out_3), .in_2(member_1_out_3), .in_3(member_2_out_3), .in_4(member_3_out_3),
    .out_5(adder_4_2_out_5));
  Comparator #(.width(3), .mode("unsigned")) comparator_1 (
    .a(adder_4_1_out_5), .b(adder_4_2_out_5), .gt(comparator_1_gt));  // open: eq, lt
  and and_1 (out_5, leader_1_out_5, comparator_1_gt);
endmodule

module Leader (
  input  [1:0] Team_Leader,
  output [2:0] out_2,
  output [2:0] out_3,
  output [2:0] out_4,
  output out_5
);

  wire decoder_1_out0, decoder_1_out1, decoder_1_out2, decoder_1_out3;

  Decoder #(.select(2)) decoder_1 (
    .out0(decoder_1_out0), .out1(decoder_1_out1), .out2(decoder_1_out2), .out3(decoder_1_out3),
    .sel(Team_Leader));  // open: en
  not not_1 (out_5, decoder_1_out3);
  assign out_2 = {{2{1'b0}}, decoder_1_out0};  // Bit_Extender bit_extender_1
  assign out_3 = {{2{1'b0}}, decoder_1_out1};  // Bit_Extender bit_extender_2
  assign out_4 = {{2{1'b0}}, decoder_1_out2};  // Bit_Extender bit_extender_3
endmodule

module Member (
  input  [1:0] Team_Member,
  output [2:0] out_2,
  output [2:0] out_3,
  output [2:0] out_4
);

  wire decoder_1_out0, decoder_1_out1, decoder_1_out2, decoder_1_out3, or_1_out;

  Decoder #(.select(2)) decoder_1 (
    .out0(decoder_1_out0), .out1(decoder_1_out1), .out2(decoder_1_out2), .out3(decoder_1_out3),
    .sel(Team_Member));  // open: en
  assign out_2 = {{2{1'b0}}, decoder_1_out0};  // Bit_Extender bit_extender_1
  or or_1 (or_1_out, decoder_1_out1, decoder_1_out3);
  assign out_3 = {{2{1'b0}}, or_1_out};  // Bit_Extender bit_extender_2
  assign out_4 = {{2{1'b0}}, decoder_1_out2};  // Bit_Extender bit_extender_3
endmodule

module adder_4 (
  input  [2:0] in_1,
  input  [2:0] in_2,
  input  [2:0] in_3,
  input  [2:0] in_4,
  output [2:0] out_5
);

  wire [2:0] adder_1_out, adder_2_out;

  Adder #(.width(3)) adder_1 (.a(in_1), .b(in_2), .out(adder_1_out));  // open: cin, cout
  Adder #(.width(3)) adder_2 (.a(adder_1_out), .b(in_3), .out(adder_2_out));  // open: cin, cout
  Adder #(.width(3)) adder_3 (.a(adder_2_out), .b(in_4), .out(out_5));  // open: cin, cout
endmodule
