// Logisim project 2.circ as structural Verilog: 3 circuits, main circuit main
module main (
  input  [1:0] in,
  input  reset,
  output [1:0] out
);

  wire clock_1_out;
  wire [2:0] nsl_1_next_state, register_1_q;

  NSL nsl_1 (.state(register_1_q), .in(in), .next_state(nsl_1_next_state));
  // Probe on nsl_1_next_state
  Register #(.width(3)) register_1 (
    .D(nsl_1_next_state), .Q(register_1_q), .clk(clock_1_out), .clr(reset));  // open: en
  Clock clock_1 (.out(clock_1_out));
  // Probe on register_1_q
  Output_Logic output_logic_1 (.state(register_1_q), .in(in), .out(out));
endmodule

module NSL (
  input  [2:0] state,
  input  [1:0] in,
  output [2:0] next_state
);

  wire and_1_out, and_2_out, and_3_out, and_4_out, and_5_out, and_6_out, and_7_out, and_8_out, and_9_out,
       and_10_out, not_1_out, not_2_out, not_3_out, not_4_out, not_5_out, not_6_out, not_7_out, not_8_out,
       not_9_out, not_10_out, not_11_out, not_12_out, not_13_out, not_14_out, not_15_out, not_16_out;

  not not_1 (not_1_out, state[2]);
  not not_2 (not_2_out, state[0]);
  not not_3 (not_3_out, state[1]);
  not not_4 (not_4_out, state[0]);
  not not_5 (not_5_out, state[2]);
  not not_6 (not_6_out, state[1]);
  not not_7 (not_7_out, in[1]);
  not not_8 (not_8_out, in[0]);
  not not_9 (not_9_out, state[2]);
  not not_10 (not_10_out, state[0]);
  not not_11 (not_11_out, in[1]);
  not not_12 (not_12_out, state[1]);
  not not_13 (not_13_out, state[0]);
  not not_14 (not_14_out, in[1]);
  not not_15 (not_15_out, state[1]);
  and and_1 (and_1_out, not_15_out, in[1]);
  and and_2 (and_2_out, state[0], in[1]);
  not not_16 (not_16_out, state[2]);
  and and_3 (and_3_out, not_16_out, state[1], in[0]);
  and and_4 (and_4_out, state[2], in[1]);
  and and_5 (and_5_out, not_1_out, state[1], not_2_out, in[1]);
  or or_1 (next_state[2], and_5_out, and_6_out, and_7_out);
  and and_6 (and_6_out, state[1], state[0], in[0]);
  and and_7 (and_7_out, state[2], not_3_out, not_4_out, in[0]);
  and and_8 (and_8_out, not_5_out, not_6_out, state[0], not_7_out, not_8_out);
  and and_9 (and_9_out, not_9_out, state[1], not_10_out, not_11_out);
  or or_2 (next_state[1], and_8_out, and_9_out, and_10_out);
  and and_10 (and_10_out, state[2], not_12_out, not_13_out, not_14_out);
  or or_3 (next_state[0], and_1_out, and_2_out, and_3_out, and_4_out);
endmodule

module Output_Logic (
  input  [2:0] state,
  input  [1:0] in,
  output [1:0] out
);

  wire not_1_out, not_2_out, not_3_out, not_4_out;

  not not_1 (not_1_out, state[1]);
  not not_2 (not_2_out, state[0]);
  not not_3 (not_3_out, in[1]);
  not not_4 (not_4_out, state[2]);
  and and_1 (out[1], state[2], not_1_out, not_2_out, not_3_out, in[0]);
  and and_2 (out[0], not_4_out, state[1], state[0], not_3_out, in[0]);
endmodule
