// Logisim project 3_2.circ as structural Verilog: 1 circuit, main circuit main
module main (
  input  [2:0] in_1,
  output [3:0] out_2
);

  wire clock_1_out, comparator_1_eq, comparator_1_lt, counter_2_q, not_1_out, or_1_out;
  wire [3:0] adder_1_out, bit_extender_1_out, counter_1_q, Fn_1_q, Fn_2_q, multiplexer_1_out, register_1_q;

  assign bit_extender_1_out = {{1{1'b0}}, in_1};  // Bit_Extender bit_extender_1
  Counter #(.width(4), .max('hf), .ongoal("stay")) counter_1 (
    .Q(counter_1_q), .clk(clock_1_out));  // open: load, D, count, carry, clr
  Counter #(.width(1), .max('h1), .ongoal("stay")) counter_2 (
    .Q(counter_2_q), .clk(clock_1_out));  // open: load, D, count, carry, clr
  Multiplexer #(.width(4)) multiplexer_1 (
    .in0(4'b0001), .in1(Fn_1_q), .out(multiplexer_1_out), .sel(counter_2_q));  // open: en
  Comparator #(.width(4), .mode("unsigned")) comparator_1 (
    .a(bit_extender_1_out), .b(counter_1_q), .eq(comparator_1_eq), .lt(comparator_1_lt));  // open: gt
  or or_1 (or_1_out, comparator_1_eq, comparator_1_lt);
  not not_1 (not_1_out, or_1_out);
  Adder #(.width(4)) adder_1 (.a(Fn_2_q), .b(multiplexer_1_out), .out(adder_1_out));  // open: cin, cout
  Register #(.width(4)) register_1 (.D(adder_1_out), .en(not_1_out), .Q(register_1_q), .clk(clock_1_out));  // open: clr
  Register #(.width(4)) Fn_1 (.D(adder_1_out), .Q(Fn_1_q), .clk(clock_1_out));  // open: en, clr
  Clock clock_1 (.out(clock_1_out));
  Register #(.width(4)) Fn_2 (.D(Fn_1_q), .Q(Fn_2_q), .clk(clock_1_out));  // open: en, clr
  Multiplexer #(.width(4)) multiplexer_2 (.in0(4'b0000), .in1(register_1_q), .out(out_2), .sel(or_1_out));  // open: en
endmodule
