// Logisim project gcd.circ as structural Verilog: 2 circuits, main circuit main
module main (
  input  [31:0] in_1,
  input  [31:0] in_2,
  input  in_3,
  output [31:0] out_4
);

  wire clk, comparator_1_eq, counter_1_q, counter_2_q, counter_3_q, not_1_out, not_2_out;
  wire [31:0] Dividend, Divisor, multiplexer_1_out, multiplexer_2_out, multiplexer_3_out, remainder_1_out_3;

  Clock clock_1 (.out(clk));
  Counter #(.width(1), .max('h1), .ongoal("stay")) counter_1 (
    .Q(counter_1_q), .clk(clk), .clr(in_3));  // open: load, D, count, carry
  Multiplexer #(.width(32)) multiplexer_1 (
    .in0(32'h1), .in1(Divisor), .out(multiplexer_1_out), .sel(counter_1_q));  // open: en
  Counter #(.width(1), .max('h1), .ongoal("stay")) counter_2 (
    .Q(counter_2_q), .clk(clk), .clr(in_3));  // open: load, D, count, carry
  Comparator #(.width(32), .mode("unsigned")) comparator_1 (
    .a(multiplexer_1_out), .b({32{1'b0}}), .eq(comparator_1_eq));  // open: gt, lt
  Multiplexer #(.width(32)) multiplexer_2 (
    .in0(in_1), .in1(Dividend), .out(multiplexer_2_out), .sel(counter_2_q));  // open: en
  Multiplexer #(.width(32)) multiplexer_3 (
    .in0(in_2), .in1(Divisor), .out(multiplexer_3_out), .sel(counter_3_q));  // open: en
  Counter #(.width(1), .max('h1), .ongoal("stay")) counter_3 (
    .Q(counter_3_q), .clk(clk), .clr(in_3));  // open: load, D, count, carry
  Remainder remainder_1 (.in_1(multiplexer_2_out), .in_2(multiplexer_3_out), .out_3(remainder_1_out_3));
  not not_1 (not_1_out, comparator_1_eq);
  not not_2 (not_2_out, comparator_1_eq);
  Register #(.width(32)) register_1 (.D(remainder_1_out_3), .en(not_1_out), .Q(Divisor), .clk(clk), .clr(in_3));
  Register #(.width(32)) register_2 (.D(multiplexer_3_out), .en(not_2_out), .Q(Dividend), .clk(clk), .clr(in_3));
  Register #(.width(32)) register_3 (.D(Dividend), .en(comparator_1_eq), .Q(out_4), .clk(clk), .clr(in_3));

  // Other names for the same wires on the sheet: A[31:0] = in_1; B[31:0] = in_2; out[31:0] = out_4; reset = in_3
endmodule

module Remainder (
  input  [31:0] in_1,
  input  [31:0] in_2,
  output [31:0] out_3
);

  Divider #(.width(32)) divider_1 (.a(in_1), .b(in_2), .rem(out_3));  // open: out, upper
endmodule
