// Logisim project single_cycle_cpu.circ as structural Verilog: 12 circuits, main circuit main
module main (
  input  in_1,
  output [31:0] out_2,
  output out_3,
  output [4:0] out_4,
  output [31:0] out_5,
  output out_6,
  output [4:0] out_7,
  output [31:0] out_8
);

  wire ALUSrc, Beq, BranchtoJump, CLK, EXTOp, lui, MemtoReg, RegDst;
  wire [1:0] DMType_1_0, JumpOp_1_0;
  wire [2:0] ALUControl_2_0;
  wire [4:0] rd_t, rs, rt, shamt;
  wire [5:0] Funct, Op;
  wire [15:0] Imm;
  wire [25:0] addr;
  wire [31:0] ALUResult, ExtendedImm, multiplexer_2_out, multiplexer_4_out, PC, PC_, RD, RD1, RD2, ReadData;

  Clock clock_1 (.out(CLK));
  Control_Unit control_unit_1 (
    .Funct(Funct), .Op(Op), .EXTOp(EXTOp), .JumpOp_1_0(JumpOp_1_0), .MemtoReg(MemtoReg), .ALUSrc(ALUSrc),
    .RegDst(RegDst), .RegWrite(out_3), .MemWrite(out_6), .ALUControl_2_0(ALUControl_2_0), .Beq(Beq),
    .DMType_1_0(DMType_1_0), .lui(lui));
  Register #(.width(32)) register_1 (.D(PC_), .Q(PC), .clk(CLK), .clr(in_1));  // open: en
  NPC npc_1 (
    .PC_31_0(PC), .SignImm_31_0(ExtendedImm), .JumpOp_1_0(JumpOp_1_0), .BranchtoJump(BranchtoJump),
    .addr_25_0(addr), .rsD(RD1), .PC__31_0(PC_));
  Splitter splitter_1 (
    .in_1(out_2), .out_2(Funct), .out_3(shamt), .out_4(rd_t), .out_5(rt), .out_6(rs), .out_7(Op),
    .out_8(Imm), .out_9(addr));
  Instruction_Memory instruction_memory_1 (.PC(PC), .Instr(out_2));
  EXT ext_1 (.in_1(EXTOp), .in_2(Imm), .Extended(ExtendedImm));
  Multiplexer #(.width(5)) multiplexer_1 (.in0(rt), .in1(rd_t), .out(out_4), .sel(RegDst));  // open: en
  Data_Memory data_memory_1 (.in_3(out_7), .in_5(out_8), .out_6(RD), .in_1(CLK), .in_2(out_6), .in_4(in_1));
  DMPreWriting dmprewriting_1 (.WriteData(RD2), .ReadData(RD), .DMType_1_0(DMType_1_0), .WriteData_(out_8));
  General_Register_File general_register_file_1 (
    .in_2(rs), .in_3(rt), .in_4(out_4), .in_5(out_5), .out_8(RD1), .out_9(RD2), .in_6(out_3), .in_7(in_1),
    .in_1(CLK));
  Multiplexer #(.width(32)) multiplexer_2 (
    .in0({ALUResult[31:7], out_7, ALUResult[1:0]}), .in1(ReadData), .out(multiplexer_2_out), .sel(MemtoReg));  // open: en
  DMPreReading dmprereading_1 (.ReadData(RD), .DMType_1_0(DMType_1_0), .ReadData_(ReadData));
  Multiplexer #(.width(32)) multiplexer_3 (
    .in0(multiplexer_2_out), .in1({Imm, {16{1'b0}}}), .out(out_5), .sel(lui));  // open: en
  ALU alu_1 (
    .in_2(RD1), .in_3(multiplexer_4_out), .out_4({ALUResult[31:7], out_7, ALUResult[1:0]}),
    .in_1(ALUControl_2_0));
  Multiplexer #(.width(32)) multiplexer_4 (
    .in0(RD2), .in1(ExtendedImm), .out(multiplexer_4_out), .sel(ALUSrc));  // open: en
  BranchIf branchif_1 (
    .beq(Beq), .bne(1'b0), .blez(1'b0), .bgtz(1'b0), .ALUResult({ALUResult[31:7], out_7, ALUResult[1:0]}),
    .BranchtoJump(BranchtoJump));

  // Other names for the same wires on the sheet: ALUResult[6:2] = out_7; imm__16_b0[31:16] = Imm; Instr[31:0] = out_2;
  //   MemWrite = out_6; RegAddr[4:0] = out_4; RegWrite = out_3; Reset = in_1; WD3[31:0] = out_5;
  //   WriteData[31:0] = out_8
endmodule

module NPC (
  input  [31:0] PC_31_0,
  input  [31:0] SignImm_31_0,
  input  [1:0] JumpOp_1_0,
  input  BranchtoJump,
  input  [25:0] addr_25_0,
  input  [31:0] rsD,
  output [31:0] PC__31_0
);

  wire [27:0] PC_4;
  wire [31:0] BranchifPC_, multiplexer_1_out, SignImm____2;
  wire [31:28] J_al__PC;

  Adder #(.width(32)) adder_1 (.a(PC_31_0), .b(32'h4), .out({J_al__PC, PC_4}));  // open: cin, cout
  Adder #(.width(32)) adder_2 (.a({J_al__PC, PC_4}), .b(SignImm____2), .out(BranchifPC_));  // open: cin, cout
  Shifter #(.width(32)) shifter_1 (.in(SignImm_31_0), .\dist (5'b00010), .out(SignImm____2));
  Multiplexer #(.width(32)) multiplexer_1 (
    .in0({J_al__PC, PC_4}), .in1(BranchifPC_), .out(multiplexer_1_out), .sel(BranchtoJump));  // open: en
  Multiplexer #(.select(2), .width(32)) multiplexer_2 (
    .in0(multiplexer_1_out), .in1({J_al__PC, addr_25_0, 2'b00}), .in2({J_al__PC, addr_25_0, 2'b00}),
    .in3(rsD), .out(PC__31_0), .sel(JumpOp_1_0));  // open: en

  // Other names for the same wires on the sheet: J_al__PC[27:2] = addr_25_0; PC_4[31:28] = J_al__PC;
  //   jr_PC[31:0] = rsD; SignImm[31:0] = SignImm_31_0

  // Notes on the sheet:
  //   jr用
endmodule

module EXT (
  input  in_1,
  input  [15:0] in_2,
  output [31:0] Extended
);

  wire [31:0] bit_extender_1_out, bit_extender_2_out;

  assign bit_extender_1_out = {{16{1'b0}}, in_2};  // Bit_Extender bit_extender_1
  assign bit_extender_2_out = {{16{in_2[15]}}, in_2};  // Bit_Extender bit_extender_2
  Multiplexer #(.width(32)) multiplexer_1 (
    .in0(bit_extender_1_out), .in1(bit_extender_2_out), .out(Extended), .sel(in_1));  // open: en

  // Other names for the same wires on the sheet: EXTSlt = in_1

  // Notes on the sheet:
  //   0: Zero
  //   1: Sign
endmodule

module Instruction_Memory (
  input  [31:0] PC,
  output [31:0] Instr
);

  ROM #(.addrWidth(5), .dataWidth(32)) rom_1 (.addr(PC[6:2]), .data(Instr));  // open: sel

  // Notes on the sheet:
  //   32 * 32  ROM
  //   contents of rom_1 (hex, n*v repeats v):
  //   8000c02 3c100064 3c110064
endmodule

module Data_Memory (
  input  in_1,
  input  in_2,
  input  [4:0] in_3,
  input  in_4,
  input  [31:0] in_5,
  output [31:0] out_6
);

  RAM #(.addrWidth(5), .dataWidth(32), .bus("separate")) ram_1 (
    .addr(in_3), .din(in_5), .data(out_6), .str(in_2), .clk(in_1), .clr(in_4));  // open: sel, ld

  // Other names for the same wires on the sheet: A[4:0] = in_3; CLK = in_1; RD[31:0] = out_6; Reset = in_4;
  //   WD[31:0] = in_5; WE = in_2

  // Notes on the sheet:
  //   32 * 32  RAM
  //   Opertating_on_Word
endmodule

module ALU (
  input  [2:0] in_1,
  input  [31:0] in_2,
  input  [31:0] in_3,
  output [31:0] out_4
);

  wire [31:0] AndResult, OrResult, Result, Result_t, Result_t_t, Result_t_t_t, Result_t_t_t_t, XOR_Result;

  assign AndResult = in_2 & in_3;  // AND_Gate and_1, 32 bits wide
  assign OrResult = in_2 | in_3;  // OR_Gate or_1, 32 bits wide
  Adder #(.width(32)) adder_1 (.a(in_2), .b(in_3), .out(Result));  // open: cin, cout
  Subtractor #(.width(32)) subtractor_1 (.a(in_2), .b(in_3), .out(Result_t));  // open: bin, bout
  assign XOR_Result = in_2 ^ in_3;  // XOR_Gate xor_1, 32 bits wide
  Shifter #(.width(32)) shifter_1 (.in(in_2), .\dist (in_3[4:0]), .out(Result_t_t));
  Shifter #(.width(32), .shift("lr")) shifter_2 (.in(in_2), .\dist (in_3[4:0]), .out(Result_t_t_t));
  Shifter #(.width(32), .shift("ar")) shifter_3 (.in(in_2), .\dist (in_3[4:0]), .out(Result_t_t_t_t));
  Multiplexer #(.select(3), .width(32)) multiplexer_1 (
    .in0(AndResult), .in1(OrResult), .in2(Result), .in3(Result_t), .in4(Result_t_t_t), .in5(Result_t_t_t_t),
    .in6(Result_t_t), .in7(XOR_Result), .out(out_4), .sel(in_1));  // open: en

  // Other names for the same wires on the sheet: ALUControl[2:0] = in_1; ALUResult[31:0] = out_4; SrcA[31:0] = in_2;
  //   SrcB[31:0] = in_3
endmodule

module General_Register_File (
  input  in_1,
  input  [4:0] in_2,
  input  [4:0] in_3,
  input  [4:0] in_4,
  input  [31:0] in_5,
  input  in_6,
  input  in_7,
  output [31:0] out_8,
  output [31:0] out_9
);

  wire [31:0] in0, in1, in2, in3, in4, in5, in6, in7, in8, in9, in10, in11, in12, in13, in14, in15, in16,
       in17, in18, in19, in20, in21, in22, in23, in24, in25, in26, in27, in28, in29, in30, in31, out0, out1,
       out2, out3, out4, out5, out6, out7, out8, out9, out10, out11, out12, out13, out14, out15, out16,
       out17, out18, out19, out20, out21, out22, out23, out24, out25, out26, out27, out28, out29, out30,
       out31;

  Register #(.width(32)) r0 (.D(in0), .en(in_6), .Q(out0), .clk(in_1), .clr(1'b1));
  Register #(.width(32)) r8 (.D(in8), .en(in_6), .Q(out8), .clk(in_1), .clr(in_7));
  Register #(.width(32)) r16 (.D(in16), .en(in_6), .Q(out16), .clk(in_1), .clr(in_7));
  Register #(.width(32)) r24 (.D(in24), .en(in_6), .Q(out24), .clk(in_1), .clr(in_7));
  Register #(.width(32)) r4 (.D(in4), .en(in_6), .Q(out4), .clk(in_1), .clr(in_7));
  Register #(.width(32)) r12 (.D(in12), .en(in_6), .Q(out12), .clk(in_1), .clr(in_7));
  Register #(.width(32)) r20 (.D(in20), .en(in_6), .Q(out20), .clk(in_1), .clr(in_7));
  Register #(.width(32)) r28 (.D(in28), .en(in_6), .Q(out28), .clk(in_1), .clr(in_7));
  Register #(.width(32)) r1 (.D(in1), .en(in_6), .Q(out1), .clk(in_1), .clr(in_7));
  Register #(.width(32)) r9 (.D(in9), .en(in_6), .Q(out9), .clk(in_1), .clr(in_7));
  Register #(.width(32)) r17 (.D(in17), .en(in_6), .Q(out17), .clk(in_1), .clr(in_7));
  Register #(.width(32)) r25 (.D(in25), .en(in_6), .Q(out25), .clk(in_1), .clr(in_7));
  Register #(.width(32)) r5 (.D(in5), .en(in_6), .Q(out5), .clk(in_1), .clr(in_7));
  Register #(.width(32)) r13 (.D(in13), .en(in_6), .Q(out13), .clk(in_1), .clr(in_7));
  Register #(.width(32)) r21 (.D(in21), .en(in_6), .Q(out21), .clk(in_1), .clr(in_7));
  Register #(.width(32)) r29 (.D(in29), .en(in_6), .Q(out29), .clk(in_1), .clr(in_7));
  Register #(.width(32)) r2 (.D(in2), .en(in_6), .Q(out2), .clk(in_1), .clr(in_7));
  Register #(.width(32)) r10 (.D(in10), .en(in_6), .Q(out10), .clk(in_1), .clr(in_7));
  Register #(.width(32)) r18 (.D(in18), .en(in_6), .Q(out18), .clk(in_1), .clr(in_7));
  Register #(.width(32)) r26 (.D(in26), .en(in_6), .Q(out26), .clk(in_1), .clr(in_7));
  Register #(.width(32)) r6 (.D(in6), .en(in_6), .Q(out6), .clk(in_1), .clr(in_7));
  Register #(.width(32)) r14 (.D(in14), .en(in_6), .Q(out14), .clk(in_1), .clr(in_7));
  Register #(.width(32)) r22 (.D(in22), .en(in_6), .Q(out22), .clk(in_1), .clr(in_7));
  Register #(.width(32)) r30 (.D(in30), .en(in_6), .Q(out30), .clk(in_1), .clr(in_7));
  Register #(.width(32)) r3 (.D(in3), .en(in_6), .Q(out3), .clk(in_1), .clr(in_7));
  Register #(.width(32)) r11 (.D(in11), .en(in_6), .Q(out11), .clk(in_1), .clr(in_7));
  Register #(.width(32)) r19 (.D(in19), .en(in_6), .Q(out19), .clk(in_1), .clr(in_7));
  Register #(.width(32)) r27 (.D(in27), .en(in_6), .Q(out27), .clk(in_1), .clr(in_7));
  Register #(.width(32)) r7 (.D(in7), .en(in_6), .Q(out7), .clk(in_1), .clr(in_7));
  Register #(.width(32)) r15 (.D(in15), .en(in_6), .Q(out15), .clk(in_1), .clr(in_7));
  Register #(.width(32)) r23 (.D(in23), .en(in_6), .Q(out23), .clk(in_1), .clr(in_7));
  Register #(.width(32)) r31 (.D(in31), .en(in_6), .Q(out31), .clk(in_1), .clr(in_7));
  Multiplexer #(.select(5), .width(32)) multiplexer_1 (
    .in0(out0), .in1(out1), .in2(out2), .in3(out3), .in4(out4), .in5(out5), .in6(out6), .in7(out7),
    .in8(out8), .in9(out9), .in10(out10), .in11(out11), .in12(out12), .in13(out13), .in14(out14),
    .in15(out15), .in16(out16), .in17(out17), .in18(out18), .in19(out19), .in20(out20), .in21(out21),
    .in22(out22), .in23(out23), .in24(out24), .in25(out25), .in26(out26), .in27(out27), .in28(out28),
    .in29(out29), .in30(out30), .in31(out31), .out(out_8), .sel(in_2));  // open: en
  Multiplexer #(.select(5), .width(32)) multiplexer_2 (
    .in0(out0), .in1(out1), .in2(out2), .in3(out3), .in4(out4), .in5(out5), .in6(out6), .in7(out7),
    .in8(out8), .in9(out9), .in10(out10), .in11(out11), .in12(out12), .in13(out13), .in14(out14),
    .in15(out15), .in16(out16), .in17(out17), .in18(out18), .in19(out19), .in20(out20), .in21(out21),
    .in22(out22), .in23(out23), .in24(out24), .in25(out25), .in26(out26), .in27(out27), .in28(out28),
    .in29(out29), .in30(out30), .in31(out31), .out(out_9), .sel(in_3));  // open: en
  Demultiplexer #(.select(5), .width(32), .tristate("true")) demultiplexer_1 (
    .out0(in0), .out1(in1), .out2(in2), .out3(in3), .out4(in4), .out5(in5), .out6(in6), .out7(in7),
    .out8(in8), .out9(in9), .out10(in10), .out11(in11), .out12(in12), .out13(in13), .out14(in14),
    .out15(in15), .out16(in16), .out17(in17), .out18(in18), .out19(in19), .out20(in20), .out21(in21),
    .out22(in22), .out23(in23), .out24(in24), .out25(in25), .out26(in26), .out27(in27), .out28(in28),
    .out29(in29), .out30(in30), .out31(in31), .in(in_5), .sel(in_4));  // open: en

  // Other names for the same wires on the sheet: A1[4:0] = in_2; A2[4:0] = in_3; A3[4:0] = in_4; CLK = in_1;
  //   RD1[31:0] = out_8; RD2[31:0] = out_9; Reset = in_7; WD3[31:0] = in_5; WE3 = in_6
endmodule

module Control_Unit (
  input  [5:0] Funct,
  input  [5:0] Op,
  output EXTOp,
  output MemtoReg,
  output ALUSrc,
  output RegDst,
  output RegWrite,
  output MemWrite,
  output Beq,
  output lui,
  output [1:0] JumpOp_1_0,
  output [1:0] DMType_1_0,
  output [2:0] ALUControl_2_0
);

  wire addu_funct_out, addu_out, J_out, Jal_out, jr_funct_out, Jr_out, lw_out, not_1_out, not_2_out,
       not_3_out, not_4_out, not_5_out, not_6_out, not_7_out, not_8_out, not_9_out, not_10_out, not_11_out,
       not_12_out, ori_out, R_out, subu_funct_out, subu_out, sw_out;

  not not_1 (not_1_out, Op[4]);
  not not_2 (not_2_out, Op[5]);
  not not_3 (not_3_out, Op[2]);
  not not_4 (not_4_out, Op[3]);
  not not_5 (not_5_out, Op[1]);
  not not_6 (not_6_out, Op[0]);
  not not_7 (not_7_out, Funct[5]);
  not not_8 (not_8_out, Funct[4]);
  not not_9 (not_9_out, Funct[2]);
  not not_10 (not_10_out, Funct[3]);
  not not_11 (not_11_out, Funct[0]);
  not not_12 (not_12_out, Funct[1]);
  and R (R_out, not_2_out, not_1_out, not_4_out, not_3_out, not_5_out, not_6_out);
  and addu_funct (addu_funct_out, Funct[5], not_8_out, not_10_out, not_9_out, not_12_out, Funct[0]);
  and subu_funct (subu_funct_out, Funct[5], not_8_out, not_10_out, not_9_out, Funct[1], Funct[0]);
  and jr_funct (jr_funct_out, not_7_out, not_8_out, Funct[3], not_9_out, not_12_out, not_11_out);
  and addu (addu_out, R_out, addu_funct_out);
  and subu (subu_out, R_out, subu_funct_out);
  and Jr (Jr_out, R_out, jr_funct_out);
  and ori (ori_out, not_2_out, not_1_out, Op[3], Op[2], not_5_out, Op[0]);
  and lw (lw_out, Op[5], not_1_out, not_4_out, not_3_out, Op[1], Op[0]);
  and sw (sw_out, Op[5], not_1_out, Op[3], not_3_out, Op[1], Op[0]);
  and u_beq (Beq, not_2_out, not_1_out, not_4_out, Op[2], not_5_out, not_6_out);
  and u_lui (lui, not_2_out, not_1_out, Op[3], Op[2], Op[1], Op[0]);
  and J (J_out, not_2_out, not_1_out, not_4_out, not_3_out, Op[1], not_6_out);
  and Jal (Jal_out, not_2_out, not_1_out, not_4_out, not_3_out, Op[1], Op[0]);
  or or_1 (EXTOp, Beq, sw_out, lw_out, 1'b0);
  or or_2 (JumpOp_1_0[1], J_out, Jr_out);
  or or_3 (JumpOp_1_0[0], Jal_out, Jr_out);
  buf or_4 (MemtoReg, lw_out);  // OR_Gate
  or or_5 (ALUSrc, lui, ori_out, sw_out, lw_out);
  or or_6 (RegDst, addu_out, subu_out);
  or or_7 (RegWrite, addu_out, subu_out, ori_out, lw_out, lui);
  buf or_8 (MemWrite, sw_out);  // OR_Gate
  or or_9 (ALUControl_2_0[2], Jr_out, lui);
  or or_10 (ALUControl_2_0[1], addu_out, subu_out, sw_out, lw_out, Beq, lui);
  or or_11 (ALUControl_2_0[0], subu_out, ori_out, Jr_out, Beq);
  buf or_12 (DMType_1_0[1], 1'b0);  // OR_Gate
  buf or_13 (DMType_1_0[0], 1'b0);  // OR_Gate

  // Notes on the sheet:
  //   不使用ALU
  //   不使用ALU
  //   Imm instead of rt
endmodule

module DMPreReading (
  input  [31:0] ReadData,
  input  [1:0] DMType_1_0,
  output [31:0] ReadData_
);

  Multiplexer #(.select(2), .width(32)) multiplexer_1 (
    .in0(ReadData), .in1({{24{1'b0}}, ReadData[7:0]}), .in2({{16{1'b0}}, ReadData[15:0]}), .out(ReadData_),
    .sel(DMType_1_0));  // open: in3, en

  // Other names for the same wires on the sheet: byte[7:0] = ReadData[7:0]; halfword[15:0] = ReadData[15:0];
  //   word[31:0] = ReadData
endmodule

module DMPreWriting (
  input  [31:0] WriteData,
  input  [31:0] ReadData,
  input  [1:0] DMType_1_0,
  output [31:0] WriteData_
);

  Multiplexer #(.select(2), .width(32)) multiplexer_1 (
    .in0(WriteData), .in1({ReadData[31:8], WriteData[7:0]}), .in2({ReadData[31:16], WriteData[15:0]}),
    .out(WriteData_), .sel(DMType_1_0));  // open: in3, en

  // Other names for the same wires on the sheet: byte[31:0] = {ReadData[31:8], WriteData[7:0]}; Read[31:0] = ReadData;
  //   halfword[31:0] = {ReadData[31:16], WriteData[15:0]}; word[31:0] = WriteData
endmodule

module Splitter (
  input  [31:0] in_1,
  output [5:0] out_2,
  output [4:0] out_3,
  output [4:0] out_4,
  output [4:0] out_5,
  output [4:0] out_6,
  output [5:0] out_7,
  output [15:0] out_8,
  output [25:0] out_9
);


  assign out_2 = in_1[5:0];
  assign out_3 = in_1[10:6];
  assign out_4 = in_1[15:11];
  assign out_5 = in_1[20:16];
  assign out_6 = in_1[25:21];
  assign out_7 = in_1[31:26];
  assign out_8 = in_1[15:0];
  assign out_9 = in_1[25:0];
endmodule

module BranchIf (
  input  beq,
  input  bne,
  input  blez,
  input  bgtz,
  input  [31:0] ALUResult,
  output BranchtoJump
);

  wire and_1_out, and_2_out, and_3_out, and_4_out, comparator_1_eq, comparator_1_gt, comparator_1_lt;

  Comparator #(.width(32)) comparator_1 (
    .a(ALUResult), .b({32{1'b0}}), .gt(comparator_1_gt), .eq(comparator_1_eq), .lt(comparator_1_lt));
  and and_1 (and_1_out, comparator_1_gt, bgtz);
  and and_2 (and_2_out, comparator_1_eq, beq);
  and and_3 (and_3_out, comparator_1_lt, blez);
  and and_4 (and_4_out, ~comparator_1_eq, bne);  // AND_Gate
  or or_1 (BranchtoJump, and_1_out, and_2_out, and_3_out, and_4_out);
endmodule
